# Fritzing sketch Smoky box (saved by Fritzing 0.9.3b)
perfboards: 1

parts:
  Part1 = nodeMCU LoLin
  Outside_temp1 = Audio Jack (TRS) 3.5mm [package="4Ucon 08780 [THT]"]  # not connected
  Smoke2 = Audio Jack (TRS) 3.5mm [package="4Ucon 08780 [THT]"]  # not connected
  Inside_temp1 = Audio Jack (TRS) 3.5mm [package="4Ucon 08780 [THT]"]  # not connected
  Power_plug3 = Power plug  # not connected
  Power_plug4 = Power plug  # not connected
  R5 = Resistor [tolerance=±5% resistance=2.2k package=THT]  # not connected
  U3 = TLP621 [package=THT]  # not connected
  LED4 = LED - 5mm [color="Green (555nm)" package="5 mm [THT]"]  # not connected
  LED5 = LED - 5mm [color="Red (635nm)" package="5 mm [THT]"]  # not connected
  Smoke3 = Audio Jack (TRS) 3.5mm [package="4Ucon 08780 [THT]"]  # not connected
  HLK-PM4 = HLK-PM01  # not connected
  R7 = Resistor [tolerance=±5% resistance=10k package="2010 [SMD]"]  # not connected
  R8 = Resistor [tolerance=±5% resistance=2.2k package="0805 [SMD]"]  # not connected
  R9 = Resistor [tolerance=±5% resistance=2.2k package=THT]  # not connected
  OMRON1 = OMRON PCB Power Relay – G5LE [part_number="G5LE-1\n" package=THT]  # not connected

nets:
  N1: Part1.VU, Part1.D10
  N2: Part1.S3, Part1.GND#32

notes:
  Inside temp
  Outside temp
  Smoke
  220V Power
  220V Heater
  Relay

custom parts:
  nodeMCU LoLin: LoLin is a tiny board, based on ESP8266, integates GPIO, PWM, IIC, 1-Wire and ADC all in one board. It's base on NodeMCU, A lua based firmware for wifi-soc esp8266 Build on ESP8266 sdk Lua core based on eLua project cjson based on lua-cjson File system based on spiffs Easy to access wireless router Based on Lua 5.1.4 (without debug, os module.) Event-Drive programming preferred. Build-in json,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
